# Fritzing sketch schaltplan (saved by Fritzing 0.9.5d)
breadboards: 1

parts:
  MH-ET_LIVE_ESP32_DEVKIT1 = MH-ET LIVE ESP32 DEVKIT 38 pins
  LED1 = LED - 5mm [color="Red (633nm)" package="5 mm [THT]"]
  R1 = Resistor [tolerance=±5% resistance=4.7k package=THT]
  Q1 = NPN-Transistor [package="TO92 [THT]"]
  DHT11 = Humidity and Temperature Sensor RHT03
  R2 = Resistor [tolerance=±5% resistance=10k package=THT]
  Relais_Modul = Keyes Relay [package=THT]
  Ultrasonic_01 = SRF05 Ultrasonic Rangefinder
  ACS712 = ACS712 Current Sensor 5A 20A 30A
  R3 = Resistor [tolerance=±5% resistance=220 package=THT]
  R4 = Resistor [tolerance=±5% resistance=220 package=THT]
  light_sensor = BH1750

nets:
  ACS712: MH-ET_LIVE_ESP32_DEVKIT1.IO34
  N1: MH-ET_LIVE_ESP32_DEVKIT1.IO14, R2.Pin_0
  N2: MH-ET_LIVE_ESP32_DEVKIT1.IO12, R1.Pin_1
  N3: MH-ET_LIVE_ESP32_DEVKIT1.GND, LED1.cathode
  GPIO13: MH-ET_LIVE_ESP32_DEVKIT1.IO13, DHT11.Data-signal
  N4: MH-ET_LIVE_ESP32_DEVKIT1.IO23, light_sensor.SDA
  N5: MH-ET_LIVE_ESP32_DEVKIT1.IO22, light_sensor.SCL
  HC-04 Echo: MH-ET_LIVE_ESP32_DEVKIT1.IO19
  HC-04 Trigger: MH-ET_LIVE_ESP32_DEVKIT1.IO18
  N6: LED1.anode, R1.Pin_0
  GND: Q1.E, DHT11.GND_2, Relais_Modul.ground, Ultrasonic_01.GND, ACS712.GND, R4.Pin_1, light_sensor.GND, light_sensor.ADDR
  N7: Q1.B, R2.Pin_1
  N8: Q1.C, Relais_Modul.signal
  5V: DHT11.Vcc, Relais_Modul.power, Ultrasonic_01.VCC, ACS712.VCC
  GPIO18: Ultrasonic_01.Trig
  GPIO19: Ultrasonic_01.Echo
  N9: ACS712.2, ACS712.OUT, R3.Pin_1, R4.Pin_0
  GPIO34: R3.Pin_0
  3.3V: light_sensor.VCC

notes:
  Hydroponic-Controller, TU Berlin Projekt Hydroponic WS22/23

custom parts:
  MH-ET LIVE ESP32 DEVKIT 38 pins: http://mh.nodebb.com/topic/2/mh-et-live-esp32-devkit
  Keyes Relay: The Keyes 5V relay module is suitable for SCM development, home appliance control. It uses a 5V~12V TIL control signal which can control DC / AC signal.
  ACS712 Current Sensor 5A 20A 30A: Remix by Michael Kubina http://www.kubina.info Original by: https://forum.fritzing.org/t/current-sensor-5a-acs712/7694 https://forum.fritzing.org/u/ArtHome ArtHome12@gmail.com
  BH1750: Light Sensor
